# Fritzing sketch weather_station_wireup_nobattery_bme280_6pin (saved by Fritzing 0.9.2b)
breadboards: 1

parts:
  U1 = NodeMCU V1.0
  R1 = PHOTOCELL [package=photocell-kit]
  R2 = Resistor [tolerance=±5% resistance=51 power=250mW part_number=100EP51451K0 package="0603 [SMD]"]

nets:
  N1: U1.3V3, R2.Pin_0
  N2: U1.GND, R1.P$1
  N3: U1.A0, R1.P$2, R2.Pin_1

custom parts:
  NodeMCU V1.0: ESP8266 based NodeMCU
